# Fritzing sketch wiring-diagram (saved by Fritzing 1.0.7)

parts:
  M1 = DOIT Esp32 DevKit v1 (30 pins long, 11 pins width) [part_number=ESP32S-PIN30]
  M2 = DC Motor [voltage_(max)=6V voltage_(min)=3V]
  MP1584EN_Board1 = MP1584EN Power Regulator Board [part_number=MP1584EN]
  VCC1 = Battery block 9V [internal_resistance=0.1Ω]
  DRV1 = DollaTek DRV8833
  M3 = DC Motor [voltage_(max)=6V voltage_(min)=3V]

nets:
  N1: M1.3V3, DRV1.pin_1
  N2: M1.D25, DRV1.pin_12
  N3: M1.D26, DRV1.pin_11
  N4: M1.D27, DRV1.pin_8
  N5: M1.D14, DRV1.pin_7
  N6: M1.GND, MP1584EN_Board1.OUT_-
  N7: M1.VIN, MP1584EN_Board1.OUT_+
  N8: M2.pin_1, DRV1.pin_3
  N9: M2.pin_2, DRV1.pin_2
  N10: MP1584EN_Board1.IN_-, VCC1.-, DRV1.pin_10
  N11: MP1584EN_Board1.IN_+, VCC1.+, DRV1.pin_9
  N12: DRV1.pin_4, M3.pin_2
  N13: DRV1.pin_5, M3.pin_1

custom parts:
  DOIT Esp32 DevKit v1 (30 pins long, 11 pins width): The DOIT Esp32 DevKit v1 is one of the development board created by DOIT to evaluate the ESP-WROOM-32 module. It is based on the ESP32 microcontroller that boasts Wifi, Bluetooth, Ethernet and Low Power support all in a single chip. (vanepp) made breadboard work, adjusted pin numbering and labels and reduced size of schematic and cleaned up pcb. This chip is 30pins long (2 x15) and 11 pins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
  MP1584EN Power Regulator Board: The MP1584EN is a high frequency step-down switching regulator. The input voltage range is 4.5V to 28V. The output voltage is set by the board's potentiometer.
  DollaTek DRV8833: DollaTek DRV8833 1.5A 2-Channel DC Motor Drive Board
